// Logisim project counter.circ as structural Verilog: 24 circuits, main circuit main
module main (
);

  wire \AUTOMÓVILES_ambar , \AUTOMÓVILES_rojo , \AUTOMÓVILES_verde , CINCO__5_2, controlador_1_control,
       controlador_2_control, controlador_3_control, decodificador_completo_1_a, decodificador_completo_1_b,
       decodificador_completo_1_c, decodificador_completo_1_d, decodificador_completo_1_e,
       decodificador_completo_1_f, decodificador_completo_1_g, decodificador_completo_2_a,
       decodificador_completo_2_b, decodificador_completo_2_c, decodificador_completo_2_d,
       decodificador_completo_2_decenas, decodificador_completo_2_e, decodificador_completo_2_f,
       decodificador_completo_2_g, DOCE__12, PEATONES_rojo, PEATONES_verde, PULSADOR_out,
       restador_cinco_1_r1, restador_cinco_1_r2, restador_cinco_1_r4, restador_cinco_1_r8,
       restador_doce_1_r1, restador_doce_1_r2, restador_doce_1_r4, restador_doce_1_r8, temporizador_1__1,
       temporizador_1__2, temporizador_1__4, temporizador_1__8, temporizador_2__1, temporizador_2__2,
       temporizador_2__4, temporizador_2__8;

  Button PULSADOR (.out(PULSADOR_out));
  controlador controlador_1 (.PULSADOR(PULSADOR_out), .RESET(DOCE__12), .CONTROL(controlador_1_control));
  controlador controlador_2 (.PULSADOR(controlador_1_control), .RESET(CINCO__5_2), .CONTROL(controlador_2_control));
  temporizador temporizador_1 (
    .PULSADOR(controlador_2_control), .RESET(CINCO__5_2), ._1(temporizador_1__1), ._2(temporizador_1__2),
    ._4(temporizador_1__4), ._8(temporizador_1__8));
  cinco CINCO (
    ._1(temporizador_1__1), ._2(temporizador_1__2), ._4(temporizador_1__4), ._5(temporizador_1__8),
    ._5_2(CINCO__5_2));
  restador__cinco restador_cinco_1 (
    .A8(temporizador_1__8), .A4(temporizador_1__4), .A2(temporizador_1__2), .A1(temporizador_1__1),
    .R1(restador_cinco_1_r1), .R2(restador_cinco_1_r2), .R4(restador_cinco_1_r4), .R8(restador_cinco_1_r8));
  decodificador_completo decodificador_completo_1 (
    .A8(restador_cinco_1_r8), .A4(restador_cinco_1_r4), .A2(restador_cinco_1_r2), .A1(restador_cinco_1_r1),
    .B(decodificador_completo_1_b), .A(decodificador_completo_1_a), .F(decodificador_completo_1_f),
    .G(decodificador_completo_1_g), .C(decodificador_completo_1_c), .D(decodificador_completo_1_d),
    .E(decodificador_completo_1_e));  // open: DECENAS
  controlador controlador_3 (.PULSADOR(CINCO__5_2), .RESET(DOCE__12), .CONTROL(controlador_3_control));
  _7_Segment_Display u_7_segment_display_1 (
    .g(decodificador_completo_1_g), .f(decodificador_completo_1_f), .a(decodificador_completo_1_a),
    .b(decodificador_completo_1_b), .e(decodificador_completo_1_e), .d(decodificador_completo_1_d),
    .c(decodificador_completo_1_c));  // open: dp
  temporizador temporizador_2 (
    .PULSADOR(controlador_3_control), .RESET(DOCE__12), ._1(temporizador_2__1), ._2(temporizador_2__2),
    ._4(temporizador_2__4), ._8(temporizador_2__8));
  doce DOCE (
    ._1(temporizador_2__1), ._2(temporizador_2__2), ._4(temporizador_2__4), ._5(temporizador_2__8),
    ._12(DOCE__12));
  restador__doce restador_doce_1 (
    .A8(temporizador_2__8), .A4(temporizador_2__4), .A2(temporizador_2__2), .A1(temporizador_2__1),
    .R1(restador_doce_1_r1), .R2(restador_doce_1_r2), .R4(restador_doce_1_r4), .R8(restador_doce_1_r8));
  \semáforo_de_automóviles  \AUTOMÓVILES  (
    .START(controlador_2_control), ._5(controlador_3_control), .RESET(DOCE__12), .ROJO(\AUTOMÓVILES_rojo ),
    .AMBAR(\AUTOMÓVILES_ambar ), .VERDE(\AUTOMÓVILES_verde ));
  semaforo_de_peatones PEATONES (
    ._5(controlador_3_control), .RESET(DOCE__12), .ROJO(PEATONES_rojo), .VERDE(PEATONES_verde));
  decodificador_completo decodificador_completo_2 (
    .A8(restador_doce_1_r8), .A4(restador_doce_1_r4), .A2(restador_doce_1_r2), .A1(restador_doce_1_r1),
    .DECENAS(decodificador_completo_2_decenas), .B(decodificador_completo_2_b),
    .A(decodificador_completo_2_a), .F(decodificador_completo_2_f), .G(decodificador_completo_2_g),
    .C(decodificador_completo_2_c), .D(decodificador_completo_2_d), .E(decodificador_completo_2_e));
  LED ROJO (.in(\AUTOMÓVILES_rojo ));
  LED AMBAR (.in(\AUTOMÓVILES_ambar ));
  LED VERDE (.in(\AUTOMÓVILES_verde ));
  LED ROJO_2 (.in(PEATONES_rojo));
  LED VERDE_2 (.in(PEATONES_verde));
  _7_Segment_Display u_7_segment_display_2 (
    .g(decodificador_completo_2_g), .f(decodificador_completo_2_f), .a(decodificador_completo_2_a),
    .b(decodificador_completo_2_b), .e(decodificador_completo_2_e), .d(decodificador_completo_2_d),
    .c(decodificador_completo_2_c));  // open: dp
  _7_Segment_Display u_7_segment_display_3 (
    .b(decodificador_completo_2_decenas), .c(decodificador_completo_2_decenas));  // open: g, f, a, e, d, dp
endmodule

// TEMPORIZADOR
module temporizador (
  input  PULSADOR,
  input  RESET,
  output _1,
  output _2,
  output _4,
  output _8
);

  wire AND_out, BIESTABLE_D_2_qn, BIESTABLE_D_3_qn, BIESTABLE_D_4_qn, BIESTABLE_D_qn, OR_out, RELOJ_out;

  Clock RELOJ (.out(RELOJ_out));
  or OR (OR_out, RESET, AND_out);
  D_Flip_Flop BIESTABLE_D (
    .clk(RELOJ_out), .D(BIESTABLE_D_qn), .Q(_1), .Qn(BIESTABLE_D_qn), .en(PULSADOR), .reset(OR_out));  // open: preset
  D_Flip_Flop BIESTABLE_D_2 (
    .clk(BIESTABLE_D_qn), .D(BIESTABLE_D_2_qn), .Q(_2), .Qn(BIESTABLE_D_2_qn), .en(PULSADOR), .reset(OR_out));  // open: preset
  D_Flip_Flop BIESTABLE_D_3 (
    .clk(BIESTABLE_D_2_qn), .D(BIESTABLE_D_3_qn), .Q(_4), .Qn(BIESTABLE_D_3_qn), .en(PULSADOR), .reset(OR_out));  // open: preset
  D_Flip_Flop BIESTABLE_D_4 (
    .clk(BIESTABLE_D_3_qn), .D(BIESTABLE_D_4_qn), .Q(_8), .Qn(BIESTABLE_D_4_qn), .en(PULSADOR), .reset(OR_out));  // open: preset
  and AND (AND_out, _4, _8);
endmodule

// CONTROLADOR
module controlador (
  input  PULSADOR,
  input  RESET,
  output CONTROL
);

  D_Flip_Flop BIESTABLE_D (.clk(PULSADOR), .D(PULSADOR), .Q(CONTROL), .en(1'b1), .reset(RESET));  // open: Qn, preset
endmodule

module semaforo_de_peatones (
  input  _5,
  input  RESET,
  output ROJO,
  output VERDE
);

  D_Flip_Flop BIESTABLE_D (.clk(_5), .D(_5), .Q(VERDE), .Qn(ROJO), .en(1'b1), .reset(RESET));  // open: preset
endmodule

module cinco (
  input  _1,
  input  _2,
  input  _4,
  input  _5,
  output _5_2
);

  and AND (_5_2, _1, ~_2, _4, ~_5);  // AND_Gate
endmodule

module doce (
  input  _1,
  input  _2,
  input  _4,
  input  _5,
  output _12
);

  and AND (_12, ~_1, ~_2, _4, _5);  // AND_Gate
endmodule

module \semáforo_de_automóviles  (
  input  START,
  input  _5,
  input  RESET,
  output ROJO,
  output AMBAR,
  output VERDE
);

  wire BIESTABLE_D_2_qn, BIESTABLE_D_q, BIESTABLE_D_qn;

  D_Flip_Flop BIESTABLE_D (
    .clk(START), .D(START), .Q(BIESTABLE_D_q), .Qn(BIESTABLE_D_qn), .en(1'b1), .reset(RESET));  // open: preset
  D_Flip_Flop BIESTABLE_D_2 (
    .clk(_5), .D(_5), .Q(ROJO), .Qn(BIESTABLE_D_2_qn), .en(1'b1), .reset(RESET));  // open: preset
  and AND (AMBAR, BIESTABLE_D_q, ~ROJO);  // AND_Gate
  and AND_2 (VERDE, BIESTABLE_D_qn, BIESTABLE_D_2_qn);
endmodule

module decodificador__decenas (
  input  A8,
  input  A4,
  input  A2,
  input  A1,
  output out_5
);

  wire OR_out;

  or OR (OR_out, A4, A2);
  and AND (out_5, A8, OR_out);
  // also tied to GND on the sheet: A1
endmodule

module decodificador__unidades (
  input  A8,
  input  A4,
  input  A2,
  input  A1,
  output B,
  output A,
  output F,
  output G,
  output C,
  output D,
  output E
);

  decodificador__B u_B (.A8(A8), .A4(A4), .A2(A2), .A1(A1), .B(B));
  decodificador__A u_A (.A8(A8), .A4(A4), .A2(A2), .A1(A1), .A(A));
  decodificador__F u_F (.A8(A8), .A4(A4), .A2(A2), .A1(A1), .F(F));
  decodificador__G u_G (.A8(A8), .A4(A4), .A2(A2), .A1(A1), .G(G));
  decodificador__C u_C (.A8(A8), .A4(A4), .A2(A2), .A1(A1), .C(C));
  decodificador__D u_D (.A8(A8), .A4(A4), .A2(A2), .A1(A1), .A(D));
  decodificador__E u_E (.A8(A8), .A4(A4), .A2(A2), .A1(A1), .E(E));
  _7_Segment_Display u_7_segment_display_1 (.g(G), .f(F), .a(A), .b(B), .e(E), .d(D), .c(C));  // open: dp
endmodule

// DECDODIFICADOR
module decodificador_completo (
  input  A8,
  input  A4,
  input  A2,
  input  A1,
  output DECENAS,
  output B,
  output A,
  output F,
  output G,
  output C,
  output D,
  output E
);

  wire rectificador_1_a1_2, rectificador_1_a2_2, rectificador_1_a4_2, rectificador_1_a8_2;

  decodificador__decenas DECODIFACOR_DECENAS (.A8(A8), .A4(A4), .A2(A2), .A1(A1), .out_5(DECENAS));
  decodificador__unidades DECODIFICADOR_UNIDADES (
    .A8(rectificador_1_a8_2), .A4(rectificador_1_a4_2), .A2(rectificador_1_a2_2), .A1(rectificador_1_a1_2),
    .B(B), .A(A), .F(F), .G(G), .C(C), .D(D), .E(E));
  rectificador rectificador_1 (
    .C(DECENAS), .A8(A8), .A4(A4), .A2(A2), .A1(A1), .A8_2(rectificador_1_a8_2), .A4_2(rectificador_1_a4_2),
    .A2_2(rectificador_1_a2_2), .A1_2(rectificador_1_a1_2));
  _7_Segment_Display u_7_segment_display_1 (.b(DECENAS), .c(DECENAS));  // open: g, f, a, e, d, dp
  _7_Segment_Display u_7_segment_display_2 (.g(G), .f(F), .a(A), .b(B), .e(E), .d(D), .c(C));  // open: dp
endmodule

module decodificador__G (
  input  A8,
  input  A4,
  input  A2,
  input  A1,
  output G
);

  wire AND_2_out, AND_3_out, AND_out, not_1_out, not_2_out, OR_out, XNOR_out;

  not not_1 (not_1_out, A2);
  not not_2 (not_2_out, A1);
  or OR (OR_out, A8, A4);
  NotExactlyOne XNOR (.out(XNOR_out), .in0(A8), .in1(A8), .in3(A4));
  and AND (AND_out, OR_out, not_1_out);
  and AND_2 (AND_2_out, XNOR_out, A2);
  and AND_3 (AND_3_out, A2, not_2_out);
  or OR_2 (G, AND_out, AND_2_out, AND_3_out);
endmodule

module decodificador__F (
  input  A8,
  input  A4,
  input  A2,
  input  A1,
  output F
);

  wire AND_out, NOR_out, OR_out, XOR_out;

  or OR (OR_out, A8, A4);
  xor XOR (XOR_out, A2, A1);
  nor NOR (NOR_out, A2, A1);
  and AND (AND_out, OR_out, XOR_out);
  or OR_2 (F, AND_out, NOR_out);
endmodule

module decodificador__E (
  input  A8,
  input  A4,
  input  A2,
  input  A1,
  output E
);

  wire AND_2_out, AND_3_out, AND_out, XNOR_2_out, XNOR_out;

  xnor XNOR (XNOR_out, A8, A4);
  xnor XNOR_2 (XNOR_2_out, A2, A1);
  and AND (AND_out, XNOR_out, ~A2, ~A1);  // AND_Gate
  and AND_2 (AND_2_out, A8, XNOR_2_out);
  and AND_3 (AND_3_out, ~A1, A2);  // AND_Gate
  or OR (E, AND_out, AND_2_out, AND_3_out);
endmodule

module decodificador__A (
  input  A8,
  input  A4,
  input  A2,
  input  A1,
  output A
);

  wire AND_2_out, AND_3_out, AND_4_out, AND_out, OR_out, XNOR_2_out, XNOR_out, XOR_out;

  xor XOR (XOR_out, A8, A4);
  or OR (OR_out, A2, A1);
  xnor XNOR (XNOR_out, A8, A4);
  xnor XNOR_2 (XNOR_2_out, A2, A1);
  and AND (AND_out, A8, ~A4);  // AND_Gate
  and AND_2 (AND_2_out, XNOR_out, XNOR_2_out);
  and AND_3 (AND_3_out, XOR_out, OR_out);
  and AND_4 (AND_4_out, A2, A2, ~A1);  // AND_Gate
  or OR_2 (A, AND_out, AND_2_out, AND_3_out, AND_4_out);
endmodule

module decodificador__B (
  input  A8,
  input  A4,
  input  A2,
  input  A1,
  output B
);

  wire XNOR_out;

  xnor XNOR (XNOR_out, A2, A1);
  or OR (B, A8, ~A4, XNOR_out);  // OR_Gate
endmodule

module decodificador__C (
  input  A8,
  input  A4,
  input  A2,
  input  A1,
  output C
);

  wire XNOR_out;

  xnor XNOR (XNOR_out, A2, A1);
  or OR (C, ~A2, A8, A4, XNOR_out);  // OR_Gate
endmodule

module decodificador__D (
  input  A8,
  input  A4,
  input  A2,
  input  A1,
  output A
);

  wire AND_2_out, AND_3_out, AND_4_out, AND_out, XNOR_2_out, XNOR_out, XOR_out;

  xor XOR (XOR_out, A2, A1);
  xnor XNOR (XNOR_out, A8, A4);
  xnor XNOR_2 (XNOR_2_out, A2, A1);
  and AND (AND_out, XOR_out, ~A8, A4);  // AND_Gate
  and AND_2 (AND_2_out, XNOR_out, XNOR_2_out);
  and AND_3 (AND_3_out, A2, ~A1);  // AND_Gate
  and AND_4 (AND_4_out, A8, ~A2, ~A1);  // AND_Gate
  or OR (A, AND_out, AND_2_out, AND_3_out, AND_4_out);
endmodule

// RECTIFICADOR
module rectificador (
  input  C,
  input  A8,
  input  A4,
  input  A2,
  input  A1,
  output A8_2,
  output A4_2,
  output A2_2,
  output A1_2
);

  wire XOR_2_out, XOR_out;

  xor XOR (XOR_out, C, A8);
  xor XOR_2 (XOR_2_out, C, A4);
  xor XOR_3 (A2_2, C, A2);
  and AND (A8_2, ~C, XOR_out);  // AND_Gate
  and AND_2 (A4_2, ~C, XOR_2_out);  // AND_Gate

  assign A1_2 = A1;
endmodule

module restador (
  input  A8,
  input  A4,
  input  A2,
  input  A1,
  input  B8,
  input  B4,
  input  B2,
  input  B1,
  output R1,
  output R2,
  output R4,
  output R8
);

  wire INVERSOR_na1, INVERSOR_na2, INVERSOR_na4, INVERSOR_na8, not_1_out, SUMADOR_2_s1, SUMADOR_2_s2,
       SUMADOR_2_s4, SUMADOR_2_s8, SUMADOR_s1, SUMADOR_s2, SUMADOR_s4, SUMADOR_s8, SUMADOR_s16;

  inversor INVERSOR (
    .A8(B8), .A4(B4), .A2(B2), .A1(B1), .CONTROL(1'b1), .nA8(INVERSOR_na8), .nA4(INVERSOR_na4),
    .nA2(INVERSOR_na2), .nA1(INVERSOR_na1));
  sumador_completo SUMADOR (
    .A8(A8), .A4(A4), .A2(A2), .A1(A1), .B8(INVERSOR_na8), .B4(INVERSOR_na4), .B2(INVERSOR_na2),
    .B1(INVERSOR_na1), .S1(SUMADOR_s1), .S2(SUMADOR_s2), .S4(SUMADOR_s4), .S8(SUMADOR_s8), .S16(SUMADOR_s16));
  sumador_completo SUMADOR_2 (
    .A8(SUMADOR_s8), .A4(SUMADOR_s4), .A2(SUMADOR_s2), .A1(SUMADOR_s1), .B8(1'b0), .B4(1'b0), .B2(1'b0),
    .B1(SUMADOR_s16), .S1(SUMADOR_2_s1), .S2(SUMADOR_2_s2), .S4(SUMADOR_2_s4), .S8(SUMADOR_2_s8));  // open: S16
  not not_1 (not_1_out, SUMADOR_s16);
  inversor INVERSOR_2 (
    .A8(SUMADOR_2_s1), .A4(SUMADOR_2_s2), .A2(SUMADOR_2_s4), .A1(SUMADOR_2_s8), .CONTROL(not_1_out),
    .nA8(R1), .nA4(R2), .nA2(R4), .nA1(R8));
endmodule

// SUMADOR
module sumador_parcial (
  input  C0,
  input  A0,
  input  B0,
  output S1,
  output C1
);

  wire AND_2_out, AND_out, XOR_2_out, XOR_out;

  xor XOR (XOR_out, C0, A0);
  xor XOR_2 (XOR_2_out, A0, B0);
  and AND (AND_out, A0, C0, C0);
  and AND_2 (AND_2_out, XOR_out, B0);
  xor XOR_3 (S1, C0, XOR_2_out);
  or OR (C1, AND_out, AND_2_out);
endmodule

module sumador_completo (
  input  A8,
  input  A4,
  input  A2,
  input  A1,
  input  B8,
  input  B4,
  input  B2,
  input  B1,
  output S1,
  output S2,
  output S4,
  output S8,
  output S16
);

  wire sumador_parcial_1_c1, sumador_parcial_2_c1, sumador_parcial_3_c1;

  sumador_parcial sumador_parcial_1 (.C0(1'b0), .A0(A1), .B0(B1), .S1(S1), .C1(sumador_parcial_1_c1));
  sumador_parcial sumador_parcial_2 (.C0(sumador_parcial_1_c1), .A0(A2), .B0(B2), .S1(S2), .C1(sumador_parcial_2_c1));
  sumador_parcial sumador_parcial_3 (.C0(sumador_parcial_2_c1), .A0(A4), .B0(B4), .S1(S4), .C1(sumador_parcial_3_c1));
  sumador_parcial sumador_parcial_4 (.C0(sumador_parcial_3_c1), .A0(A8), .B0(B8), .S1(S8), .C1(S16));
endmodule

module inversor (
  input  A8,
  input  A4,
  input  A2,
  input  A1,
  input  CONTROL,
  output nA8,
  output nA4,
  output nA2,
  output nA1
);

  xor XOR (nA8, A8, CONTROL);
  xor XOR_2 (nA4, A4, CONTROL);
  xor XOR_3 (nA2, A2, CONTROL);
  xor XOR_4 (nA1, A1, CONTROL);
endmodule

module restador__doce (
  input  A8,
  input  A4,
  input  A2,
  input  A1,
  output R1,
  output R2,
  output R4,
  output R8
);

  wire doce_1__12;

  restador RESTADOR (
    .A8(1'b1), .A4(1'b1), .A2(1'b0), .A1(1'b0), .B8(A8), .B4(A4), .B2(A2), .B1(A1), .R1(R1), .R2(R2),
    .R4(R4), .R8(R8));
  doce doce_1 (._1(R8), ._2(R4), ._4(R2), ._5(R1), ._12(doce_1__12));
endmodule

module restador__cinco (
  input  A8,
  input  A4,
  input  A2,
  input  A1,
  output R1,
  output R2,
  output R4,
  output R8
);

  restador RESTADOR (
    .A8(1'b0), .A4(1'b1), .A2(1'b0), .A1(1'b1), .B8(A8), .B4(A4), .B2(A2), .B1(A1), .R1(R1), .R2(R2),
    .R4(R4), .R8(R8));
endmodule
