// Logisim project voting.circ as structural Verilog: 9 circuits, main circuit main
module main (
  input  AZUL,
  input  ROJO,
  input  A0,
  input  A1,
  input  A2,
  input  A3,
  input  A4,
  input  R0,
  input  R1,
  input  R2,
  input  R3,
  input  R1_2,
  input  in_13,
  input  in_14,
  input  in_15,
  input  in_16,
  input  in_17,
  input  in_18,
  input  in_19,
  input  in_20,
  input  in_21,
  input  in_22,
  input  in_23,
  input  in_24,
  input  in_25,
  input  in_26,
  input  in_27,
  input  in_28,
  input  in_29,
  input  in_30,
  input  in_31,
  input  in_32,
  output AZUL_2,
  output ROJO_2
);

  wire codificador_completo_1__1, codificador_completo_1__1_2, codificador_completo_1__2,
       codificador_completo_1__2_2, codificador_completo_1__4, codificador_completo_1__4_2,
       codificador_completo_2__1, codificador_completo_2__1_2, codificador_completo_2__2,
       codificador_completo_2__2_2, codificador_completo_2__4, codificador_completo_2__4_2,
       codificador_completo_3__1, codificador_completo_3__1_2, codificador_completo_3__2_2,
       codificador_completo_3__4, codificador_completo_3__4_2, comparador_con_desempate_1_azul_2,
       comparador_con_desempate_1_rojo_2, sumador_completo_1__1, sumador_completo_1__2,
       sumador_completo_1__4, sumador_completo_1__8, sumador_completo_2__1, sumador_completo_2__2,
       sumador_completo_2__4, sumador_completo_2__8, undriven, undriven_2, undriven_3, undriven_4,
       undriven_5, undriven_6, undriven_7, undriven_8, undriven_9, undriven_10, undriven_11, undriven_12,
       undriven_13, undriven_14, undriven_15, undriven_16, undriven_17, undriven_18, undriven_19,
       undriven_20, undriven_21, undriven_22, undriven_23, undriven_24, undriven_25, undriven_26,
       undriven_27, undriven_28, undriven_29, undriven_30, undriven_31, undriven_32;

  codificador_completo codificador_completo_1 (
    .A1(undriven), .A2(undriven_4), .A3(undriven_7), .A4(undriven_10), .A5(undriven_14), .R1(undriven_18),
    .R2(undriven_21), .R3(undriven_24), .R4(undriven_27), .R5(undriven_30), ._1(codificador_completo_1__1),
    ._2(codificador_completo_1__2), ._4(codificador_completo_1__4), ._1_2(codificador_completo_1__1_2),
    ._2_2(codificador_completo_1__2_2), ._4_2(codificador_completo_1__4_2));
  codificador_completo codificador_completo_2 (
    .A1(undriven_2), .A2(undriven_5), .A3(undriven_8), .A4(undriven_11), .A5(undriven_15), .R1(undriven_19),
    .R2(undriven_22), .R3(undriven_25), .R4(undriven_28), .R5(undriven_31), ._1(codificador_completo_2__1),
    ._2(codificador_completo_2__2), ._4(codificador_completo_2__4), ._1_2(codificador_completo_2__1_2),
    ._2_2(codificador_completo_2__2_2), ._4_2(codificador_completo_2__4_2));
  codificador_completo codificador_completo_3 (
    .A1(undriven_3), .A2(undriven_6), .A3(undriven_9), .A4(undriven_12), .A5(undriven_16), .R1(undriven_20),
    .R2(undriven_23), .R3(undriven_26), .R4(undriven_29), .R5(undriven_32), ._1(codificador_completo_3__1),
    ._2(codificador_completo_3__1), ._4(codificador_completo_3__4), ._1_2(codificador_completo_3__1_2),
    ._2_2(codificador_completo_3__2_2), ._4_2(codificador_completo_3__4_2));
  sumador_completo sumador_completo_1 (
    .A1(codificador_completo_1__1), .A2(codificador_completo_1__2), .A3(codificador_completo_1__4),
    .A4(codificador_completo_2__1), .A5(codificador_completo_2__2), .A6(codificador_completo_2__4),
    .A7(codificador_completo_3__1), .A8(codificador_completo_3__1), .A9(codificador_completo_3__4),
    ._1(sumador_completo_1__1), ._2(sumador_completo_1__2), ._4(sumador_completo_1__4),
    ._8(sumador_completo_1__8));
  sumador_completo sumador_completo_2 (
    .A1(codificador_completo_1__1_2), .A2(codificador_completo_1__2_2), .A3(codificador_completo_1__4_2),
    .A4(codificador_completo_2__1_2), .A5(codificador_completo_2__2_2), .A6(codificador_completo_2__4_2),
    .A7(codificador_completo_3__1_2), .A8(codificador_completo_3__2_2), .A9(codificador_completo_3__4_2),
    ._1(sumador_completo_2__1), ._2(sumador_completo_2__2), ._4(sumador_completo_2__4),
    ._8(sumador_completo_2__8));
  comparador__con_desempate comparador_con_desempate_1 (
    .AZUL(undriven_13), .ROJO(undriven_17), .A1(sumador_completo_1__1), .A2(sumador_completo_1__2),
    .A4(sumador_completo_1__4), .A8(sumador_completo_1__8), .R1(sumador_completo_2__1),
    .R2(sumador_completo_2__2), .R4(sumador_completo_2__4), .R8(sumador_completo_2__8),
    .AZUL_2(comparador_con_desempate_1_azul_2), .ROJO_2(comparador_con_desempate_1_rojo_2));
endmodule

// 2
module codificador_parcial (
  input  _0,
  input  _1,
  input  _2,
  input  _3,
  input  _4,
  output _1_2,
  output _2_2,
  output _4_2
);

  wire AND_2_out, AND_out, not_1_out, not_2_out, OR_out;

  not not_1 (not_1_out, _2);
  not not_2 (not_2_out, _4);
  or OR (OR_out, _2, _3);
  and AND (AND_out, _1, not_1_out, not_1_out);
  and AND_2 (AND_2_out, _3, not_2_out);
  and AND_3 (_2_2, not_2_out, OR_out);
  or OR_2 (_1_2, AND_out, AND_2_out);

  assign _4_2 = _4;
  // also tied to GND on the sheet: _0
endmodule

// CODIFICADOR
module codificador_completo (
  input  A1,
  input  A2,
  input  A3,
  input  A4,
  input  A5,
  input  R1,
  input  R2,
  input  R3,
  input  R4,
  input  R5,
  output _1,
  output _2,
  output _4,
  output _1_2,
  output _2_2,
  output _4_2
);

  codificador_parcial DECO (._0(A1), ._1(A2), ._2(A3), ._3(A4), ._4(A5), ._1_2(_1), ._2_2(_2), ._4_2(_4));
  codificador_parcial DECO_2 (._0(R1), ._1(R2), ._2(R3), ._3(R4), ._4(R5), ._1_2(_1_2), ._2_2(_2_2), ._4_2(_4_2));
endmodule

// SUMADOR
module sumador_parcial (
  input  C0,
  input  A0,
  input  B0,
  output S1,
  output C1
);

  wire AND_2_out, AND_out, XOR_2_out, XOR_out;

  xor XOR (XOR_out, C0, A0);
  xor XOR_2 (XOR_2_out, A0, B0);
  and AND (AND_out, A0, C0, C0);
  and AND_2 (AND_2_out, XOR_out, B0);
  xor XOR_3 (S1, C0, XOR_2_out);
  or OR (C1, AND_out, AND_2_out);
endmodule

// SUMADOR
module sumador_completo (
  input  A1,
  input  A2,
  input  A3,
  input  A4,
  input  A5,
  input  A6,
  input  A7,
  input  A8,
  input  A9,
  output _1,
  output _2,
  output _4,
  output _8
);

  wire sumador_2_jueces_1__1, sumador_2_jueces_1__2, sumador_2_jueces_1__4, sumador_2_jueces_1__8,
       sumador_2_jueces_2__8;

  sumador_2_jueces sumador_2_jueces_1 (
    .A1(A1), .A4(A2), .A2(A4), .A5(A5), .A3(A7), .A7(A8), ._1(sumador_2_jueces_1__1),
    ._2(sumador_2_jueces_1__2), ._4(sumador_2_jueces_1__4), ._8(sumador_2_jueces_1__8));
  sumador_2_jueces sumador_2_jueces_2 (
    .A1(sumador_2_jueces_1__1), .A4(A3), .A2(sumador_2_jueces_1__2), .A5(A6), .A3(sumador_2_jueces_1__4),
    .A7(A9), ._1(_1), ._2(_2), ._4(_4), ._8(sumador_2_jueces_2__8));
  or OR (_8, sumador_2_jueces_2__8, sumador_2_jueces_1__8);
endmodule

// SUMADOR
module sumador_2_jueces (
  input  A1,
  input  A4,
  input  A2,
  input  A5,
  input  A3,
  input  A7,
  output _1,
  output _2,
  output _4,
  output _8
);

  wire sumador_parcial_1_c1, sumador_parcial_2_c1;

  sumador_parcial sumador_parcial_1 (.C0(1'b0), .A0(A1), .B0(A4), .S1(_1), .C1(sumador_parcial_1_c1));
  sumador_parcial sumador_parcial_2 (.C0(sumador_parcial_1_c1), .A0(A2), .B0(A5), .S1(_2), .C1(sumador_parcial_2_c1));
  sumador_parcial sumador_parcial_3 (.C0(sumador_parcial_2_c1), .A0(A3), .B0(A7), .S1(_4), .C1(_8));
endmodule

// COMPADOR
module comparador_parcial (
  input  CONTROL,
  input  A,
  input  R,
  output AZUL,
  output EMPATE,
  output ROJO
);

  wire not_1_out, not_2_out, not_3_out, OR_out;

  not not_1 (not_1_out, A);
  xor OR (OR_out, A, R);
  not not_2 (not_2_out, R);
  not not_3 (not_3_out, OR_out);
  and AND (AZUL, CONTROL, A, not_2_out);
  and AND_2 (EMPATE, CONTROL, not_3_out);
  and AND_3 (ROJO, CONTROL, not_1_out, R);
endmodule

// COMPARADOR
module comparador_completo (
  input  A8,
  input  R8,
  input  A4,
  input  R4,
  input  A2,
  input  R2,
  input  A1,
  input  R1,
  output AZUL,
  output ROJI,
  output AZUL_2,
  output ROJO,
  output AZU,
  output ROJO_2,
  output AZUL_3,
  output ROJO_3,
  output EMPATE
);

  wire comparador_parcial_1_empate, comparador_parcial_2_empate, comparador_parcial_3_empate;

  comparador_parcial comparador_parcial_1 (
    .CONTROL(1'b1), .A(A8), .R(R8), .AZUL(AZUL), .EMPATE(comparador_parcial_1_empate), .ROJO(ROJI));
  comparador_parcial comparador_parcial_2 (
    .CONTROL(comparador_parcial_1_empate), .A(A4), .R(R4), .AZUL(AZUL_2),
    .EMPATE(comparador_parcial_2_empate), .ROJO(ROJO));
  comparador_parcial comparador_parcial_3 (
    .CONTROL(comparador_parcial_2_empate), .A(A2), .R(R2), .AZUL(AZU), .EMPATE(comparador_parcial_3_empate),
    .ROJO(ROJO_2));
  comparador_parcial comparador_parcial_4 (
    .CONTROL(comparador_parcial_3_empate), .A(A1), .R(R1), .AZUL(AZUL_3), .EMPATE(EMPATE), .ROJO(ROJO_3));
endmodule

module comparador__con_desempate (
  input  AZUL,
  input  ROJO,
  input  A1,
  input  A2,
  input  A4,
  input  A8,
  input  R1,
  input  R2,
  input  R4,
  input  R8,
  output AZUL_2,
  output ROJO_2
);

  wire AND_2_out, AND_out, comparador_completo_1_azu, comparador_completo_1_azul,
       comparador_completo_1_azul_2, comparador_completo_1_azul_3, comparador_completo_1_empate,
       comparador_completo_1_roji, comparador_completo_1_rojo, comparador_completo_1_rojo_2,
       comparador_completo_1_rojo_3;

  comparador_completo comparador_completo_1 (
    .A8(A8), .R8(R8), .A4(A4), .R4(R4), .A2(A2), .R2(R2), .A1(A1), .R1(R1),
    .AZUL(comparador_completo_1_azul), .ROJI(comparador_completo_1_roji),
    .AZUL_2(comparador_completo_1_azul_2), .ROJO(comparador_completo_1_rojo),
    .AZU(comparador_completo_1_azu), .ROJO_2(comparador_completo_1_rojo_2),
    .AZUL_3(comparador_completo_1_azul_3), .ROJO_3(comparador_completo_1_rojo_3),
    .EMPATE(comparador_completo_1_empate));
  and AND (AND_out, comparador_completo_1_empate, AZUL);
  and AND_2 (AND_2_out, ROJO, comparador_completo_1_empate);
  or OR (AZUL_2, AND_out, comparador_completo_1_azul, comparador_completo_1_azul_2, comparador_completo_1_azu, comparador_completo_1_azul_3);
  or OR_2 (ROJO_2, AND_2_out, comparador_completo_1_roji, comparador_completo_1_rojo, comparador_completo_1_rojo_2, comparador_completo_1_rojo_3);
endmodule
